// Logisim project 64位二进制快速加法器.circ as structural Verilog: 1 circuit, main circuit Adder64
// 加法器
module Adder64 (
  input  Cin,
  input  [31:0] X,
  input  [31:0] X_2,
  input  [31:0] Y,
  input  [31:0] Y_2,
  output CF,
  output OF,
  output Cout,
  output SF,
  output ZF,
  output [31:0] S,
  output [31:0] S_2
);

  wire and_1_out, and_2_out, and_3_out, and_4_out, and_5_out, and_6_out, and_7_out, comparator_1_eq,
       comparator_2_eq, main_2_gg, main_2_pg, main_3_gg, main_3_pg, main_4_gg, main_4_pg, not_1_out,
       not_2_out, not_3_out, or_1_out, or_2_out, or_4_out;

  xor xor_1 (CF, Cout, Cin);
  not not_1 (not_1_out, X[31]);
  not not_2 (not_2_out, S[31]);
  lab4_2_main main_1 (.X(X[31:16]), .Y(Y[31:16]), .C0(or_1_out), .S(S[31:16]), .C16(Cout));  // open: Pg, Gg
  or or_1 (or_1_out, main_2_gg, and_1_out);
  not not_3 (not_3_out, Y[31]);
  and and_1 (and_1_out, or_2_out, main_2_pg);
  and and_2 (and_2_out, Y[31], X[31]);
  and and_3 (and_3_out, and_2_out, not_2_out);
  and and_4 (and_4_out, not_3_out, not_1_out);
  lab4_2_main main_2 (
    .X(X[15:0]), .Y(Y[15:0]), .C0(or_2_out), .S(S[15:0]), .Pg(main_2_pg), .Gg(main_2_gg));  // open: C16
  or or_2 (or_2_out, main_3_gg, and_6_out);
  or or_3 (OF, and_3_out, and_5_out);
  and and_5 (and_5_out, and_4_out, S[31]);
  Comparator #(.width(32), .mode("unsigned")) comparator_1 (
    .a(S), .b({32{1'b0}}), .eq(comparator_1_eq));  // open: gt, lt
  and and_6 (and_6_out, or_4_out, main_3_pg);
  // Probe on X
  // Probe on Y
  // Probe on S
  lab4_2_main main_3 (
    .X(X_2[31:16]), .Y(Y_2[31:16]), .C0(or_4_out), .S(S_2[31:16]), .Pg(main_3_pg), .Gg(main_3_gg));  // open: C16
  or or_4 (or_4_out, main_4_gg, and_7_out);
  and and_7 (and_7_out, Cin, main_4_pg);
  // Probe on X_2
  // Probe on Y_2
  // Probe on S_2
  lab4_2_main main_4 (
    .X(X_2[15:0]), .Y(Y_2[15:0]), .C0(Cin), .S(S_2[15:0]), .Pg(main_4_pg), .Gg(main_4_gg));  // open: C16
  Comparator #(.width(32), .mode("unsigned")) comparator_2 (
    .a(S_2), .b({32{1'b0}}), .eq(comparator_2_eq));  // open: gt, lt
  and and_8 (ZF, comparator_1_eq, comparator_2_eq);

  assign SF = S[31];

  // Other names for the same wires on the sheet: S1[31:0] = S; S0[31:0] = S_2; X0[31:0] = X_2; X1[31:0] = X;
  //   Y0[31:0] = Y_2; Y1[31:0] = Y

  // Notes on the sheet:
  //   Y: pull=down
  //   Cin: pull=down
  //   X_2: pull=down
  //   X: pull=down
  //   Y_2: pull=down
  //   输入引脚区
  //   输出引脚区
  //   请勿修改引脚名称、电路名称及电路封装外观
  //   提示：使用16位并行加法器子电路实现32位快速加法器
  //   功能说明:32位Adder  S=X+Y，Cout为最高位进位位，Cin为进位输入， S为和，溢出OF、进位CF、零ZF、符号SF。
  //   +
  //   =
  //   无符号加法
endmodule
